// Logisim project main.circ as structural Verilog: 2 circuits, main circuit main
module main (
  input  Input_A,
  input  in_2,
  output Output
);

  and and_1 (Output, Input_A, in_2);

  // Notes on the sheet:
  //   AND Gate
  //   Roll Number - 79
  //   Cse 18
  //   Name - LOVE YADAV
endmodule

module Exp_1 (
  input  in_1,
  input  Input_B,
  output Output
);

  or or_1 (Output, in_1, Input_B);

  // Notes on the sheet:
  //   OR Gate
  //   Cse 18
  //   Name - LOVE YADAV
  //   Roll Number - 79
endmodule
